# Fritzing sketch Absen Real-Time_Kelompok 2 (saved by Fritzing 0.9.3b)
breadboards: 1

parts:
  M1 = DOIT Esp32 DevKit v1 (30 pins long, 11 pins width) [part_number=ESP32S-PIN30]
  Part1 = Fingerprint Sensor
  Part2 = LCD1602-I2C
  Part3 = Adafruit DS3231 [part_number="Adafruit #3013"]
  Part4 = LilyPad Buzzer

nets:
  3V3: M1.3V3, Part1.VCC, Part3.Vin
  GND: M1.GND, Part1.GND, Part2.GND, Part4.-
  N1: M1.RX2, Part1.TX
  N2: M1.TX2, Part1.RX
  N3: M1.D18, Part4.+
  N4: M1.D21, Part2.SDA, Part3.SDA
  N5: M1.D22, Part2.SCL, Part3.SCL
  VIN: M1.VIN, Part2.VCC

custom parts:
  DOIT Esp32 DevKit v1 (30 pins long, 11 pins width): The DOIT Esp32 DevKit v1 is one of the development board created by DOIT to evaluate the ESP-WROOM-32 module. It is based on the ESP32 microcontroller that boasts Wifi, Bluetooth, Ethernet and Low Power support all in a single chip. (vanepp) made breadboard work, adjusted pin numbering and labels and reduced size of schematic and cleaned up pcb. This chip is 30pins long (2 x15) and 11 pins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
  Fingerprint Sensor: FINGERPRIN Sensor
  LCD1602-I2C: A standard character display, usually with 2x16 characters. Comes in many colors with LCM1602 IIC attached.
  Adafruit DS3231: The datasheet for the DS3231 explains that this part is an "Extremely Accurate I²C-Integrated RTC/TCXO/Crystal". And, hey, it does exactly what it says on the tin! This Real Time Clock (RTC) is the most precise you can get in a small, low power package. Most RTCs use an external 32kHz timing crystal that is used to keep time with low current draw. And that's all well and good, but those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
